# Fritzing sketch device_with_solar (saved by Fritzing 0.9.3b)
breadboards: 1

parts:
  Part1 = Arduino Uno (Rev3)
  HC-SR04 = HC-SR04 Ultrasonic Distance Sensor
  U1 = LIPO-2000mAh [package=lipo-2000]

nets:
  N1: Part1.D10_PWM/SS, HC-SR04.ECHO
  N2: Part1.D11_PWM/MOSI, HC-SR04.TRIG
  GND: Part1.GND, HC-SR04.GND, U1.-
  N3: Part1.VIN, U1.+

notes:
  Solar LiPo Charger Module
  VERTER 5v USB Buck-Boost Module
  DC Source
